# Fritzing sketch ChristmasLight (saved by Fritzing 0.9.2b)
breadboards: 1
stripboards: 1

parts:
  J-Power = male pin header, 2 pins [form="♂ (male)"]
  R4 = Resistor [tolerance=±5% resistance=10k package=THT]
  R6 = Resistor [tolerance=±5% resistance=330 package=THT]
  C3 = Electrolytic Capacitor [capacitance=1µF package="100 mil [THT, electrolytic]"]
  J-LEDStripe = male pin header, 3 pins [form="♂ (male)"]
  R1 = Resistor [tolerance=±5% resistance=10k package=THT]
  C2 = Electrolytic Capacitor [capacitance=1mF package="100 mil [THT, electrolytic]"]
  J-Action = male pin header, 2 pins [form="♂ (male)"]
  U1 = attiny85 [package=dip]
  C1 = Ceramic Capacitor [capacitance=22µF voltage=6.3V package="100 mil [THT, multilayer]"]

nets:
  5V: J-Power.pin1, R4.Pin_0, C3.+, J-LEDStripe.pin1, R1.Pin_0, C2.+, U1.Pin_8
  GND: J-Power.pin2, C3.-, J-LEDStripe.pin3, C2.-, J-Action.pin2, U1.Pin_4, C1.0
  N1: R4.Pin_1, J-Action.pin1, U1.Pin_7
  N2: R6.Pin_0, U1.Pin_3
  N3: R6.Pin_1, J-LEDStripe.pin2
  N4: R1.Pin_1, U1.Pin_1, C1.1
